# Fritzing sketch microphone (saved by Fritzing 0.9.0b)
breadboards: 1

parts:
  MIC1 = Microphone
  Part1 = Arduino Uno (Rev3)

nets:
  N1: MIC1.pin2, Part1.A1

notes:
  microphone (A0)
  INPUT_PULLUP
